// Logisim project CUBEPUTER.circ as structural Verilog: 12 circuits, main circuit main
module main (
);

  wire clk_out, Reset_out;
  wire [1:0] inst_cmd;
  wire [23:0] InstToCube_column1, InstToCube_column2, InstToCube_column3, InstToCube_column4,
       InstToCube_column5, InstToCube_column6, InstToCube_column7, InstToCube_column8, InstToCube_column9,
       InstToCube_column10, InstToCube_column11, InstToCube_column12, InstToCube_column13,
       InstToCube_column14, InstToCube_column15, InstToCube_column16, InstToCube_column17,
       InstToCube_column18, InstToCube_column19, InstToCube_column20, InstToCube_column21,
       InstToCube_column22, InstToCube_column23, InstToCube_column24;

  Clock clk (.out(clk_out));
  Button Reset (.out(Reset_out));
  CPU inst (.clock(clk_out), .start(Reset_out), .cmd(inst_cmd));
  GPU InstToCube (
    .inst(inst_cmd), .clk(clk_out), .Load(Reset_out), .Column1(InstToCube_column1),
    .Column2(InstToCube_column2), .Column3(InstToCube_column3), .Column4(InstToCube_column4),
    .Column5(InstToCube_column5), .Column6(InstToCube_column6), .Column7(InstToCube_column7),
    .Column8(InstToCube_column8), .Column9(InstToCube_column9), .Column10(InstToCube_column10),
    .Column11(InstToCube_column11), .Column12(InstToCube_column12), .Column13(InstToCube_column13),
    .Column14(InstToCube_column14), .Column15(InstToCube_column15), .Column16(InstToCube_column16),
    .Column17(InstToCube_column17), .Column18(InstToCube_column18), .Column19(InstToCube_column19),
    .Column20(InstToCube_column20), .Column21(InstToCube_column21), .Column22(InstToCube_column22),
    .Column23(InstToCube_column23), .Column24(InstToCube_column24));
  DotMatrix #(.matrixcols(24), .matrixrows(24)) Screen (
    .col0(InstToCube_column1), .col1(InstToCube_column2), .col2(InstToCube_column3),
    .col3(InstToCube_column4), .col4(InstToCube_column5), .col5(InstToCube_column6),
    .col6(InstToCube_column7), .col7(InstToCube_column8), .col8(InstToCube_column9),
    .col9(InstToCube_column10), .col10(InstToCube_column11), .col11(InstToCube_column12),
    .col12(InstToCube_column13), .col13(InstToCube_column14), .col14(InstToCube_column15),
    .col15(InstToCube_column16), .col16(InstToCube_column17), .col17(InstToCube_column18),
    .col18(InstToCube_column19), .col19(InstToCube_column20), .col20(InstToCube_column21),
    .col21(InstToCube_column22), .col22(InstToCube_column23), .col23(InstToCube_column24));
endmodule

module CPU (
  input  clock,
  input  start,
  output [1:0] cmd
);

  wire nor_1_out, or_1_out;
  wire [3:0] counter_1_q;

  Counter #(.max('hf), .width(4)) counter_1 (
    .load(1'b0), .D(4'b0000), .count(1'b1), .Q(counter_1_q), .up(1'b1), .clk(clock), .clr(or_1_out));  // open: carry
  or or_1 (or_1_out, start, nor_1_out);
  ROM #(.addrWidth(4), .dataWidth(2)) inst (.addr(counter_1_q), .data(cmd));
  nor nor_1 (nor_1_out, cmd[0], cmd[1]);

  // Notes on the sheet:
  //   contents of inst (hex, n*v repeats v):
  //   4*2 3
endmodule

module Pixel_Register (
  input  [1:0] cmd,
  input  clock,
  input  Load,
  output [9:0] Point1,
  output [9:0] Point2,
  output [9:0] Point3,
  output [9:0] Point4,
  output [9:0] Point5,
  output [9:0] Point6,
  output [9:0] Point7,
  output [9:0] Point8,
  output [9:0] Point9,
  output [9:0] Point10,
  output [9:0] Point11,
  output [9:0] Point12,
  output [9:0] Point13,
  output [9:0] Point14,
  output [9:0] Point15,
  output [9:0] Point16,
  output [9:0] Point17,
  output [9:0] Point18,
  output [9:0] Point19,
  output [9:0] Point20,
  output [9:0] Point21,
  output [9:0] Point22,
  output [9:0] Point23,
  output [9:0] Point24,
  output [9:0] Point25,
  output [9:0] Point26,
  output [9:0] Point27,
  output [9:0] Point28,
  output [9:0] Point29,
  output [9:0] Point30,
  output [9:0] Point31,
  output [9:0] Point32,
  output [9:0] Point33,
  output [9:0] Point34,
  output [9:0] Point35,
  output [9:0] Point36,
  output [9:0] Point37,
  output [9:0] Point38,
  output [9:0] Point39,
  output [9:0] Point40,
  output [9:0] Point41,
  output [9:0] Point42,
  output [9:0] Point43,
  output [9:0] Point44,
  output [9:0] Point45,
  output [9:0] Point46,
  output [9:0] Point47,
  output [9:0] Point48,
  output [9:0] Point49,
  output [9:0] Point50,
  output [9:0] Point51,
  output [9:0] Point52,
  output [9:0] Point53,
  output [9:0] Point54,
  output [9:0] Point55,
  output [9:0] Point56,
  output [9:0] Point57,
  output [9:0] Point58,
  output [9:0] Point59,
  output [9:0] Point60,
  output [9:0] Point61,
  output [9:0] Point62,
  output [9:0] Point63,
  output [9:0] Point64,
  output [9:0] Point65,
  output [9:0] Point66,
  output [9:0] Point67,
  output [9:0] Point68,
  output [9:0] Point69,
  output [9:0] Point70,
  output [9:0] Point71,
  output [9:0] Point72,
  output [9:0] Point73,
  output [9:0] Point74,
  output [9:0] Point75,
  output [9:0] Point76,
  output [9:0] Point77,
  output [9:0] Point78,
  output [9:0] Point79,
  output [9:0] Point80,
  output [9:0] Point81,
  output [9:0] Point82,
  output [9:0] Point83,
  output [9:0] Point84,
  output [9:0] Point85,
  output [9:0] Point86,
  output [9:0] Point87,
  output [9:0] Point88,
  output [9:0] Point89,
  output [9:0] Point90,
  output [9:0] Point91,
  output [9:0] Point92,
  output [9:0] Point93,
  output [9:0] Point94,
  output [9:0] Point95,
  output [9:0] Point96,
  output [9:0] Point97,
  output [9:0] Point98,
  output [9:0] Point99,
  output [9:0] Point100,
  output [9:0] Point101,
  output [9:0] Point102,
  output [9:0] Point103,
  output [9:0] Point104,
  output [9:0] Point105,
  output [9:0] Point106,
  output [9:0] Point107,
  output [9:0] Point108,
  output [9:0] Point109,
  output [9:0] Point110,
  output [9:0] Point111,
  output [9:0] Point112,
  output [9:0] Point113,
  output [9:0] Point114,
  output [9:0] Point115,
  output [9:0] Point116,
  output [9:0] Point117,
  output [9:0] Point118,
  output [9:0] Point119,
  output [9:0] Point120,
  output [9:0] Point121,
  output [9:0] Point122,
  output [9:0] Point123,
  output [9:0] Point124,
  output [9:0] Point125,
  output [9:0] Point126,
  output [9:0] Point127,
  output [9:0] Point128
);

  pixel pixel_1 (.cmd(cmd), .Init(54'h11170445c11170), .clk(clock), .Load(Load), .Point(Point1));
  pixel pixel_2 (.cmd(cmd), .Init(54'h11170445c249f0), .clk(clock), .Load(Load), .Point(Point9));
  pixel pixel_3 (.cmd(cmd), .Init(54'h1117061a811170), .clk(clock), .Load(Load), .Point(Point17));
  pixel pixel_4 (.cmd(cmd), .Init(54'h1117088b811170), .clk(clock), .Load(Load), .Point(Point25));
  pixel pixel_5 (.cmd(cmd), .Init(54'h11170afc811170), .clk(clock), .Load(Load), .Point(Point33));
  pixel pixel_6 (.cmd(cmd), .Init(54'h11170afc8249f0), .clk(clock), .Load(Load), .Point(Point41));
  pixel pixel_7 (.cmd(cmd), .Init(54'h15f90445c11170), .clk(clock), .Load(Load), .Point(Point49));
  pixel pixel_8 (.cmd(cmd), .Init(54'h1adb0445c11170), .clk(clock), .Load(Load), .Point(Point57));
  pixel pixel_9 (.cmd(cmd), .Init(54'h1fbd0445c11170), .clk(clock), .Load(Load), .Point(Point65));
  pixel pixel_10 (.cmd(cmd), .Init(54'h249f0445c11170), .clk(clock), .Load(Load), .Point(Point73));
  pixel pixel_11 (.cmd(cmd), .Init(54'h29810445c11170), .clk(clock), .Load(Load), .Point(Point81));
  pixel pixel_12 (.cmd(cmd), .Init(54'h2bf20445c1adb0), .clk(clock), .Load(Load), .Point(Point89));
  pixel pixel_13 (.cmd(cmd), .Init(54'h2bf204e2011170), .clk(clock), .Load(Load), .Point(Point97));
  pixel pixel_14 (.cmd(cmd), .Init(54'h2bf20753011170), .clk(clock), .Load(Load), .Point(Point105));
  pixel pixel_15 (.cmd(cmd), .Init(54'h2bf209c4011170), .clk(clock), .Load(Load), .Point(Point113));
  pixel pixel_16 (.cmd(cmd), .Init(54'h2bf20afc81adb0), .clk(clock), .Load(Load), .Point(Point121));
  pixel pixel_17 (.cmd(cmd), .Init(54'h11170445c13880), .clk(clock), .Load(Load), .Point(Point2));
  pixel pixel_18 (.cmd(cmd), .Init(54'h11170445c27100), .clk(clock), .Load(Load), .Point(Point10));
  pixel pixel_19 (.cmd(cmd), .Init(54'h1117061a82bf20), .clk(clock), .Load(Load), .Point(Point18));
  pixel pixel_20 (.cmd(cmd), .Init(54'h1117088b82bf20), .clk(clock), .Load(Load), .Point(Point26));
  pixel pixel_21 (.cmd(cmd), .Init(54'h11170afc813880), .clk(clock), .Load(Load), .Point(Point34));
  pixel pixel_22 (.cmd(cmd), .Init(54'h11170afc827100), .clk(clock), .Load(Load), .Point(Point42));
  pixel pixel_23 (.cmd(cmd), .Init(54'h15f90445c2bf20), .clk(clock), .Load(Load), .Point(Point50));
  pixel pixel_24 (.cmd(cmd), .Init(54'h1adb0445c2bf20), .clk(clock), .Load(Load), .Point(Point58));
  pixel pixel_25 (.cmd(cmd), .Init(54'h1fbd0445c2bf20), .clk(clock), .Load(Load), .Point(Point66));
  pixel pixel_26 (.cmd(cmd), .Init(54'h249f0445c2bf20), .clk(clock), .Load(Load), .Point(Point74));
  pixel pixel_27 (.cmd(cmd), .Init(54'h29810445c2bf20), .clk(clock), .Load(Load), .Point(Point82));
  pixel pixel_28 (.cmd(cmd), .Init(54'h2bf20445c1d4c0), .clk(clock), .Load(Load), .Point(Point90));
  pixel pixel_29 (.cmd(cmd), .Init(54'h2bf204e202bf20), .clk(clock), .Load(Load), .Point(Point98));
  pixel pixel_30 (.cmd(cmd), .Init(54'h2bf2075302bf20), .clk(clock), .Load(Load), .Point(Point106));
  pixel pixel_31 (.cmd(cmd), .Init(54'h2bf209c402bf20), .clk(clock), .Load(Load), .Point(Point114));
  pixel pixel_32 (.cmd(cmd), .Init(54'h2bf20afc81d4c0), .clk(clock), .Load(Load), .Point(Point122));
  pixel pixel_33 (.cmd(cmd), .Init(54'h11170445c15f90), .clk(clock), .Load(Load), .Point(Point3));
  pixel pixel_34 (.cmd(cmd), .Init(54'h11170445c29810), .clk(clock), .Load(Load), .Point(Point11));
  pixel pixel_35 (.cmd(cmd), .Init(54'h111706b6c11170), .clk(clock), .Load(Load), .Point(Point19));
  pixel pixel_36 (.cmd(cmd), .Init(54'h11170927c11170), .clk(clock), .Load(Load), .Point(Point27));
  pixel pixel_37 (.cmd(cmd), .Init(54'h11170afc815f90), .clk(clock), .Load(Load), .Point(Point35));
  pixel pixel_38 (.cmd(cmd), .Init(54'h11170afc829810), .clk(clock), .Load(Load), .Point(Point43));
  pixel pixel_39 (.cmd(cmd), .Init(54'h15f90afc811170), .clk(clock), .Load(Load), .Point(Point51));
  pixel pixel_40 (.cmd(cmd), .Init(54'h1adb0afc811170), .clk(clock), .Load(Load), .Point(Point59));
  pixel pixel_41 (.cmd(cmd), .Init(54'h1fbd0afc811170), .clk(clock), .Load(Load), .Point(Point67));
  pixel pixel_42 (.cmd(cmd), .Init(54'h249f0afc811170), .clk(clock), .Load(Load), .Point(Point75));
  pixel pixel_43 (.cmd(cmd), .Init(54'h29810afc811170), .clk(clock), .Load(Load), .Point(Point83));
  pixel pixel_44 (.cmd(cmd), .Init(54'h2bf20445c1fbd0), .clk(clock), .Load(Load), .Point(Point91));
  pixel pixel_45 (.cmd(cmd), .Init(54'h2bf2057e411170), .clk(clock), .Load(Load), .Point(Point99));
  pixel pixel_46 (.cmd(cmd), .Init(54'h2bf207ef411170), .clk(clock), .Load(Load), .Point(Point107));
  pixel pixel_47 (.cmd(cmd), .Init(54'h2bf20a60411170), .clk(clock), .Load(Load), .Point(Point115));
  pixel pixel_48 (.cmd(cmd), .Init(54'h2bf20afc81fbd0), .clk(clock), .Load(Load), .Point(Point123));
  pixel pixel_49 (.cmd(cmd), .Init(54'h11170445c186a0), .clk(clock), .Load(Load), .Point(Point4));
  pixel pixel_50 (.cmd(cmd), .Init(54'h11170445c2bf20), .clk(clock), .Load(Load), .Point(Point12));
  pixel pixel_51 (.cmd(cmd), .Init(54'h111706b6c2bf20), .clk(clock), .Load(Load), .Point(Point20));
  pixel pixel_52 (.cmd(cmd), .Init(54'h11170927c2bf20), .clk(clock), .Load(Load), .Point(Point28));
  pixel pixel_53 (.cmd(cmd), .Init(54'h11170afc8186a0), .clk(clock), .Load(Load), .Point(Point36));
  pixel pixel_54 (.cmd(cmd), .Init(54'h11170afc82bf20), .clk(clock), .Load(Load), .Point(Point44));
  pixel pixel_55 (.cmd(cmd), .Init(54'h15f90afc82bf20), .clk(clock), .Load(Load), .Point(Point52));
  pixel pixel_56 (.cmd(cmd), .Init(54'h1adb0afc82bf20), .clk(clock), .Load(Load), .Point(Point60));
  pixel pixel_57 (.cmd(cmd), .Init(54'h1fbd0afc82bf20), .clk(clock), .Load(Load), .Point(Point68));
  pixel pixel_58 (.cmd(cmd), .Init(54'h249f0afc82bf20), .clk(clock), .Load(Load), .Point(Point76));
  pixel pixel_59 (.cmd(cmd), .Init(54'h29810afc82bf20), .clk(clock), .Load(Load), .Point(Point84));
  pixel pixel_60 (.cmd(cmd), .Init(54'h2bf20445c222e0), .clk(clock), .Load(Load), .Point(Point92));
  pixel pixel_61 (.cmd(cmd), .Init(54'h2bf2057e42bf20), .clk(clock), .Load(Load), .Point(Point100));
  pixel pixel_62 (.cmd(cmd), .Init(54'h2bf207ef42bf20), .clk(clock), .Load(Load), .Point(Point108));
  pixel pixel_63 (.cmd(cmd), .Init(54'h2bf20a6042bf20), .clk(clock), .Load(Load), .Point(Point116));
  pixel pixel_64 (.cmd(cmd), .Init(54'h2bf20afc8222e0), .clk(clock), .Load(Load), .Point(Point124));
  pixel pixel_65 (.cmd(cmd), .Init(54'h11170445c1adb0), .clk(clock), .Load(Load), .Point(Point5));
  pixel pixel_66 (.cmd(cmd), .Init(54'h111704e2011170), .clk(clock), .Load(Load), .Point(Point13));
  pixel pixel_67 (.cmd(cmd), .Init(54'h11170753011170), .clk(clock), .Load(Load), .Point(Point21));
  pixel pixel_68 (.cmd(cmd), .Init(54'h111709c4011170), .clk(clock), .Load(Load), .Point(Point29));
  pixel pixel_69 (.cmd(cmd), .Init(54'h11170afc81adb0), .clk(clock), .Load(Load), .Point(Point37));
  pixel pixel_70 (.cmd(cmd), .Init(54'h13880445c11170), .clk(clock), .Load(Load), .Point(Point45));
  pixel pixel_71 (.cmd(cmd), .Init(54'h186a0445c11170), .clk(clock), .Load(Load), .Point(Point53));
  pixel pixel_72 (.cmd(cmd), .Init(54'h1d4c0445c11170), .clk(clock), .Load(Load), .Point(Point61));
  pixel pixel_73 (.cmd(cmd), .Init(54'h222e0445c11170), .clk(clock), .Load(Load), .Point(Point69));
  pixel pixel_74 (.cmd(cmd), .Init(54'h27100445c11170), .clk(clock), .Load(Load), .Point(Point77));
  pixel pixel_75 (.cmd(cmd), .Init(54'h2bf20445c11170), .clk(clock), .Load(Load), .Point(Point85));
  pixel pixel_76 (.cmd(cmd), .Init(54'h2bf20445c249f0), .clk(clock), .Load(Load), .Point(Point93));
  pixel pixel_77 (.cmd(cmd), .Init(54'h2bf2061a811170), .clk(clock), .Load(Load), .Point(Point101));
  pixel pixel_78 (.cmd(cmd), .Init(54'h2bf2088b811170), .clk(clock), .Load(Load), .Point(Point109));
  pixel pixel_79 (.cmd(cmd), .Init(54'h2bf20afc811170), .clk(clock), .Load(Load), .Point(Point117));
  pixel pixel_80 (.cmd(cmd), .Init(54'h2bf20afc8249f0), .clk(clock), .Load(Load), .Point(Point125));
  pixel pixel_81 (.cmd(cmd), .Init(54'h11170445c1d4c0), .clk(clock), .Load(Load), .Point(Point6));
  pixel pixel_82 (.cmd(cmd), .Init(54'h111704e202bf20), .clk(clock), .Load(Load), .Point(Point14));
  pixel pixel_83 (.cmd(cmd), .Init(54'h1117075302bf20), .clk(clock), .Load(Load), .Point(Point22));
  pixel pixel_84 (.cmd(cmd), .Init(54'h111709c402bf20), .clk(clock), .Load(Load), .Point(Point30));
  pixel pixel_85 (.cmd(cmd), .Init(54'h11170afc81d4c0), .clk(clock), .Load(Load), .Point(Point38));
  pixel pixel_86 (.cmd(cmd), .Init(54'h13880445c2bf20), .clk(clock), .Load(Load), .Point(Point46));
  pixel pixel_87 (.cmd(cmd), .Init(54'h186a0445c2bf20), .clk(clock), .Load(Load), .Point(Point54));
  pixel pixel_88 (.cmd(cmd), .Init(54'h1d4c0445c2bf20), .clk(clock), .Load(Load), .Point(Point62));
  pixel pixel_89 (.cmd(cmd), .Init(54'h222e0445c2bf20), .clk(clock), .Load(Load), .Point(Point70));
  pixel pixel_90 (.cmd(cmd), .Init(54'h27100445c2bf20), .clk(clock), .Load(Load), .Point(Point78));
  pixel pixel_91 (.cmd(cmd), .Init(54'h2bf20445c13880), .clk(clock), .Load(Load), .Point(Point86));
  pixel pixel_92 (.cmd(cmd), .Init(54'h2bf20445c27100), .clk(clock), .Load(Load), .Point(Point94));
  pixel pixel_93 (.cmd(cmd), .Init(54'h2bf2061a82bf20), .clk(clock), .Load(Load), .Point(Point102));
  pixel pixel_94 (.cmd(cmd), .Init(54'h2bf2088b82bf20), .clk(clock), .Load(Load), .Point(Point110));
  pixel pixel_95 (.cmd(cmd), .Init(54'h2bf20afc813880), .clk(clock), .Load(Load), .Point(Point118));
  pixel pixel_96 (.cmd(cmd), .Init(54'h2bf20afc827100), .clk(clock), .Load(Load), .Point(Point126));
  pixel pixel_97 (.cmd(cmd), .Init(54'h11170445c1fbd0), .clk(clock), .Load(Load), .Point(Point7));
  pixel pixel_98 (.cmd(cmd), .Init(54'h1117057e411170), .clk(clock), .Load(Load), .Point(Point15));
  pixel pixel_99 (.cmd(cmd), .Init(54'h111707ef411170), .clk(clock), .Load(Load), .Point(Point23));
  pixel pixel_100 (.cmd(cmd), .Init(54'h11170a60411170), .clk(clock), .Load(Load), .Point(Point31));
  pixel pixel_101 (.cmd(cmd), .Init(54'h11170afc81fbd0), .clk(clock), .Load(Load), .Point(Point39));
  pixel pixel_102 (.cmd(cmd), .Init(54'h13880afc811170), .clk(clock), .Load(Load), .Point(Point47));
  pixel pixel_103 (.cmd(cmd), .Init(54'h186a0afc811170), .clk(clock), .Load(Load), .Point(Point55));
  pixel pixel_104 (.cmd(cmd), .Init(54'h1d4c0afc811170), .clk(clock), .Load(Load), .Point(Point63));
  pixel pixel_105 (.cmd(cmd), .Init(54'h222e0afc811170), .clk(clock), .Load(Load), .Point(Point71));
  pixel pixel_106 (.cmd(cmd), .Init(54'h27100afc811170), .clk(clock), .Load(Load), .Point(Point79));
  pixel pixel_107 (.cmd(cmd), .Init(54'h2bf20445c15f90), .clk(clock), .Load(Load), .Point(Point87));
  pixel pixel_108 (.cmd(cmd), .Init(54'h2bf20445c29810), .clk(clock), .Load(Load), .Point(Point95));
  pixel pixel_109 (.cmd(cmd), .Init(54'h2bf206b6c11170), .clk(clock), .Load(Load), .Point(Point103));
  pixel pixel_110 (.cmd(cmd), .Init(54'h2bf20927c11170), .clk(clock), .Load(Load), .Point(Point111));
  pixel pixel_111 (.cmd(cmd), .Init(54'h2bf20afc815f90), .clk(clock), .Load(Load), .Point(Point119));
  pixel pixel_112 (.cmd(cmd), .Init(54'h2bf20afc829810), .clk(clock), .Load(Load), .Point(Point127));
  pixel pixel_113 (.cmd(cmd), .Init(54'h11170445c222e0), .clk(clock), .Load(Load), .Point(Point8));
  pixel pixel_114 (.cmd(cmd), .Init(54'h1117057e42bf20), .clk(clock), .Load(Load), .Point(Point16));
  pixel pixel_115 (.cmd(cmd), .Init(54'h111707ef42bf20), .clk(clock), .Load(Load), .Point(Point24));
  pixel pixel_116 (.cmd(cmd), .Init(54'h11170a6042bf20), .clk(clock), .Load(Load), .Point(Point32));
  pixel pixel_117 (.cmd(cmd), .Init(54'h11170afc8222e0), .clk(clock), .Load(Load), .Point(Point40));
  pixel pixel_118 (.cmd(cmd), .Init(54'h13880afc82bf20), .clk(clock), .Load(Load), .Point(Point48));
  pixel pixel_119 (.cmd(cmd), .Init(54'h186a0afc82bf20), .clk(clock), .Load(Load), .Point(Point56));
  pixel pixel_120 (.cmd(cmd), .Init(54'h1d4c0afc82bf20), .clk(clock), .Load(Load), .Point(Point64));
  pixel pixel_121 (.cmd(cmd), .Init(54'h222e0afc82bf20), .clk(clock), .Load(Load), .Point(Point72));
  pixel pixel_122 (.cmd(cmd), .Init(54'h27100afc82bf20), .clk(clock), .Load(Load), .Point(Point80));
  pixel pixel_123 (.cmd(cmd), .Init(54'h2bf20445c186a0), .clk(clock), .Load(Load), .Point(Point88));
  pixel pixel_124 (.cmd(cmd), .Init(54'h2bf20445c2bf20), .clk(clock), .Load(Load), .Point(Point96));
  pixel pixel_125 (.cmd(cmd), .Init(54'h2bf206b6c2bf20), .clk(clock), .Load(Load), .Point(Point104));
  pixel pixel_126 (.cmd(cmd), .Init(54'h2bf20927c2bf20), .clk(clock), .Load(Load), .Point(Point112));
  pixel pixel_127 (.cmd(cmd), .Init(54'h2bf20afc8186a0), .clk(clock), .Load(Load), .Point(Point120));
  pixel pixel_128 (.cmd(cmd), .Init(54'h2bf20afc82bf20), .clk(clock), .Load(Load), .Point(Point128));

  // Other names for the same wires on the sheet: clk = clock
endmodule

module pixel (
  input  [1:0] cmd,
  input  [53:0] Init,
  input  clk,
  input  Load,
  output [9:0] Point
);

  wire [17:5] divider_1_out, divider_2_out;
  wire [53:0] multiplexer_1_out, multiplexer_2_out, P1_q, plusx_1_new_coordinate, plusy_1_new_coordinate;

  PlusX plusx_1 (.Old_Coordinate(P1_q), .New_Coordinate(plusx_1_new_coordinate));
  PlusY plusy_1 (.Old_Coordinate(P1_q), .New_Coordinate(plusy_1_new_coordinate));
  Multiplexer #(.select(2), .width(54)) multiplexer_1 (
    .in0(P1_q), .in1(P1_q), .in2(plusx_1_new_coordinate), .in3(plusy_1_new_coordinate),
    .out(multiplexer_1_out), .sel(cmd));
  Multiplexer #(.width(54)) multiplexer_2 (.in0(multiplexer_1_out), .in1(Init), .out(multiplexer_2_out), .sel(Load));
  Register #(.width(54)) P1 (.D(multiplexer_2_out), .en(clk), .clk(clk), .Q(P1_q));  // open: clr
  Divider #(.width(18)) divider_1 (
    .a(P1_q[17:0]), .b(18'h2710), .out({divider_1_out, Point[4:0]}));  // open: upper, rem
  Divider #(.width(18)) divider_2 (
    .a(P1_q[35:18]), .b(18'h2710), .out({divider_2_out, Point[9:5]}));  // open: upper, rem
endmodule

module PlusX (
  input  [53:0] Old_Coordinate,
  output [53:0] New_Coordinate
);

  wire [47:0] adder_1_out, CenteredY, CenteredZ, divider_1_out, divider_2_out, multiplier_1_out,
       multiplier_2_out, multiplier_3_out, multiplier_4_out, subtractor_3_out;
  wire [47:18] adder_2_out, adder_3_out;

  Subtractor #(.width(48)) subtractor_1 (
    .a({{30{1'b0}}, Old_Coordinate[35:18]}), .b(48'h1d4c0), .out(CenteredY));  // open: bin, bout
  Subtractor #(.width(48)) subtractor_2 (
    .a({{30{1'b0}}, Old_Coordinate[53:36]}), .b(48'h1d4c0), .out(CenteredZ));  // open: bin, bout
  Multiplier #(.mode("twosComplement"), .width(48)) multiplier_1 (
    .a(CenteredY), .b(48'hf3363), .out(multiplier_1_out));  // open: cin, cout
  Multiplier #(.mode("twosComplement"), .width(48)) multiplier_2 (
    .a(CenteredZ), .b(48'h15474), .out(multiplier_2_out));  // open: cin, cout
  Multiplier #(.mode("twosComplement"), .width(48)) multiplier_3 (
    .a(CenteredY), .b(48'h15474), .out(multiplier_3_out));  // open: cin, cout
  Multiplier #(.mode("twosComplement"), .width(48)) multiplier_4 (
    .a(CenteredZ), .b(48'hf3363), .out(multiplier_4_out));  // open: cin, cout
  Subtractor #(.width(48)) subtractor_3 (
    .a(multiplier_1_out), .b(multiplier_2_out), .out(subtractor_3_out));  // open: bin, bout
  Adder #(.width(48)) adder_1 (.a(multiplier_3_out), .b(multiplier_4_out), .out(adder_1_out));  // open: cin, cout
  Divider #(.mode("twosComplement"), .width(48)) divider_1 (
    .a(subtractor_3_out), .b(48'hf4240), .out(divider_1_out));  // open: upper, rem
  Divider #(.mode("twosComplement"), .width(48)) divider_2 (
    .a(adder_1_out), .b(48'hf4240), .out(divider_2_out));  // open: upper, rem
  Adder #(.width(48)) adder_2 (
    .a(divider_1_out), .b(48'h1d4c0), .out({adder_2_out, New_Coordinate[35:18]}));  // open: cin, cout
  Adder #(.width(48)) adder_3 (
    .a(divider_2_out), .b(48'h1d4c0), .out({adder_3_out, New_Coordinate[53:36]}));  // open: cin, cout

  assign New_Coordinate[17:0] = Old_Coordinate[17:0];

  // Other names for the same wires on the sheet: newY[17:0] = New_Coordinate[35:18];
  //   newZ[17:0] = New_Coordinate[53:36]; x[17:0] = Old_Coordinate[17:0]; y[17:0] = Old_Coordinate[35:18];
  //   z[17:0] = Old_Coordinate[53:36]
endmodule

module PlusY (
  input  [53:0] Old_Coordinate,
  output [53:0] New_Coordinate
);

  wire [47:0] adder_1_out, CenteredX, CenteredZ, divider_1_out, divider_2_out, multiplier_1_out,
       multiplier_2_out, multiplier_3_out, multiplier_4_out, subtractor_3_out;
  wire [47:18] adder_2_out, adder_3_out;

  Subtractor #(.width(48)) subtractor_1 (
    .a({{30{1'b0}}, Old_Coordinate[17:0]}), .b(48'h1d4c0), .out(CenteredX));  // open: bin, bout
  Subtractor #(.width(48)) subtractor_2 (
    .a({{30{1'b0}}, Old_Coordinate[53:36]}), .b(48'h1d4c0), .out(CenteredZ));  // open: bin, bout
  Multiplier #(.mode("twosComplement"), .width(48)) multiplier_1 (
    .a(CenteredX), .b(48'hf3363), .out(multiplier_1_out));  // open: cin, cout
  Multiplier #(.mode("twosComplement"), .width(48)) multiplier_2 (
    .a(CenteredZ), .b(48'h15474), .out(multiplier_2_out));  // open: cin, cout
  Multiplier #(.mode("twosComplement"), .width(48)) multiplier_3 (
    .a(CenteredZ), .b(48'hf3363), .out(multiplier_3_out));  // open: cin, cout
  Multiplier #(.mode("twosComplement"), .width(48)) multiplier_4 (
    .a(CenteredX), .b(48'h15474), .out(multiplier_4_out));  // open: cin, cout
  Adder #(.width(48)) adder_1 (.a(multiplier_1_out), .b(multiplier_2_out), .out(adder_1_out));  // open: cin, cout
  Subtractor #(.width(48)) subtractor_3 (
    .a(multiplier_3_out), .b(multiplier_4_out), .out(subtractor_3_out));  // open: bin, bout
  Divider #(.mode("twosComplement"), .width(48)) divider_1 (
    .a(adder_1_out), .b(48'hf4240), .out(divider_1_out));  // open: upper, rem
  Divider #(.mode("twosComplement"), .width(48)) divider_2 (
    .a(subtractor_3_out), .b(48'hf4240), .out(divider_2_out));  // open: upper, rem
  Adder #(.width(48)) adder_2 (
    .a(divider_1_out), .b(48'h1d4c0), .out({adder_2_out, New_Coordinate[17:0]}));  // open: cin, cout
  Adder #(.width(48)) adder_3 (
    .a(divider_2_out), .b(48'h1d4c0), .out({adder_3_out, New_Coordinate[53:36]}));  // open: cin, cout

  assign New_Coordinate[35:18] = Old_Coordinate[35:18];

  // Other names for the same wires on the sheet: newX[17:0] = New_Coordinate[17:0];
  //   newZ[17:0] = New_Coordinate[53:36]; y[17:0] = Old_Coordinate[35:18]; x[17:0] = Old_Coordinate[17:0];
  //   z[17:0] = Old_Coordinate[53:36]
endmodule

module Interpreter (
  input  [9:0] in_1,
  input  [9:0] in_2,
  input  [9:0] in_3,
  input  [9:0] in_4,
  input  [9:0] in_5,
  input  [9:0] in_6,
  input  [9:0] in_7,
  input  [9:0] in_8,
  input  [9:0] in_9,
  input  [9:0] in_10,
  input  [9:0] in_11,
  input  [9:0] in_12,
  input  [9:0] in_13,
  input  [9:0] in_14,
  input  [9:0] in_15,
  input  [9:0] in_16,
  input  [9:0] in_17,
  input  [9:0] in_18,
  input  [9:0] in_19,
  input  [9:0] in_20,
  input  [9:0] in_21,
  input  [9:0] in_22,
  input  [9:0] in_23,
  input  [9:0] in_24,
  input  [9:0] in_25,
  input  [9:0] in_26,
  input  [9:0] in_27,
  input  [9:0] in_28,
  input  [9:0] in_29,
  input  [9:0] in_30,
  input  [9:0] in_31,
  input  [9:0] in_32,
  input  [9:0] in_33,
  input  [9:0] in_34,
  input  [9:0] in_35,
  input  [9:0] in_36,
  input  [9:0] in_37,
  input  [9:0] in_38,
  input  [9:0] in_39,
  input  [9:0] in_40,
  input  [9:0] in_41,
  input  [9:0] in_42,
  input  [9:0] in_43,
  input  [9:0] in_44,
  input  [9:0] in_45,
  input  [9:0] in_46,
  input  [9:0] in_47,
  input  [9:0] in_48,
  input  [9:0] in_49,
  input  [9:0] in_50,
  input  [9:0] in_51,
  input  [9:0] in_52,
  input  [9:0] in_53,
  input  [9:0] in_54,
  input  [9:0] in_55,
  input  [9:0] in_56,
  input  [9:0] in_57,
  input  [9:0] in_58,
  input  [9:0] in_59,
  input  [9:0] in_60,
  input  [9:0] in_61,
  input  [9:0] in_62,
  input  [9:0] in_63,
  input  [9:0] in_64,
  input  [9:0] in_65,
  input  [9:0] in_66,
  input  [9:0] in_67,
  input  [9:0] in_68,
  input  [9:0] in_69,
  input  [9:0] in_70,
  input  [9:0] in_71,
  input  [9:0] in_72,
  input  [9:0] in_73,
  input  [9:0] in_74,
  input  [9:0] in_75,
  input  [9:0] in_76,
  input  [9:0] in_77,
  input  [9:0] in_78,
  input  [9:0] in_79,
  input  [9:0] in_80,
  input  [9:0] in_81,
  input  [9:0] in_82,
  input  [9:0] in_83,
  input  [9:0] in_84,
  input  [9:0] in_85,
  input  [9:0] in_86,
  input  [9:0] in_87,
  input  [9:0] in_88,
  input  [9:0] in_89,
  input  [9:0] in_90,
  input  [9:0] in_91,
  input  [9:0] in_92,
  input  [9:0] in_93,
  input  [9:0] in_94,
  input  [9:0] in_95,
  input  [9:0] in_96,
  input  [9:0] in_97,
  input  [9:0] in_98,
  input  [9:0] in_99,
  input  [9:0] in_100,
  input  [9:0] in_101,
  input  [9:0] in_102,
  input  [9:0] in_103,
  input  [9:0] in_104,
  input  [9:0] in_105,
  input  [9:0] in_106,
  input  [9:0] in_107,
  input  [9:0] in_108,
  input  [9:0] in_109,
  input  [9:0] in_110,
  input  [9:0] in_111,
  input  [9:0] in_112,
  input  [9:0] in_113,
  input  [9:0] in_114,
  input  [9:0] in_115,
  input  [9:0] in_116,
  input  [9:0] in_117,
  input  [9:0] in_118,
  input  [9:0] in_119,
  input  [9:0] in_120,
  input  [9:0] in_121,
  input  [9:0] in_122,
  input  [9:0] in_123,
  input  [9:0] in_124,
  input  [9:0] in_125,
  input  [9:0] in_126,
  input  [9:0] in_127,
  input  [9:0] in_128,
  output [23:0] out_129,
  output [23:0] out_130,
  output [23:0] out_131,
  output [23:0] out_132,
  output [23:0] out_133,
  output [23:0] out_134,
  output [23:0] out_135,
  output [23:0] out_136,
  output [23:0] out_137,
  output [23:0] out_138,
  output [23:0] out_139,
  output [23:0] out_140,
  output [23:0] out_141,
  output [23:0] out_142,
  output [23:0] out_143,
  output [23:0] out_144,
  output [23:0] out_145,
  output [23:0] out_146,
  output [23:0] out_147,
  output [23:0] out_148,
  output [23:0] out_149,
  output [23:0] out_150,
  output [23:0] out_151,
  output [23:0] out_152
);

  wire [23:0] O11, O12, O13, O14, O15, O16, O17, O18, O19, O21, O22, O23, O24, O25, O26, O27, O28, O29, O110,
       O111, O112, O113, O114, O115, O116, O117, O118, O119, O120, O121, O122, O123, O124, O210, O211, O212,
       O213, O214, O215, O216, O217, O218, O219, O220, O221, O222, O223, O224;

  third4 third4_1 (
    .I1(in_1), .I2(in_2), .I3(in_3), .I4(in_4), .I5(in_5), .I6(in_6), .I7(in_7), .I8(in_8), .I9(in_9),
    .I10(in_10), .I11(in_11), .I12(in_12), .I13(in_13), .I14(in_14), .I15(in_15), .I16(in_16), .I17(in_17),
    .in_18(in_18), .in_19(in_19), .in_20(in_20), .in_21(in_21), .in_22(in_22), .in_23(in_23), .in_24(in_24),
    .in_25(in_25), .in_26(in_26), .in_27(in_27), .in_28(in_28), .in_29(in_29), .in_30(in_30), .in_31(in_31),
    .in_32(in_32), .I33(in_33), .in_34(in_34), .in_35(in_35), .in_36(in_36), .in_37(in_37), .in_38(in_38),
    .in_39(in_39), .in_40(in_40), .in_41(in_41), .in_42(in_42), .in_43(in_43), .in_44(in_44), .in_45(in_45),
    .in_46(in_46), .in_47(in_47), .in_48(in_48), .I49(in_49), .in_50(in_50), .in_51(in_51), .in_52(in_52),
    .in_53(in_53), .in_54(in_54), .in_55(in_55), .in_56(in_56), .in_57(in_57), .in_58(in_58), .in_59(in_59),
    .in_60(in_60), .in_61(in_61), .in_62(in_62), .in_63(in_63), .in_64(in_64), .O1(O11), .O2(O12), .O3(O13),
    .O4(O14), .O5(O15), .O6(O16), .O7(O17), .O8(O18), .O9(O19), .O10(O110), .O11(O111), .O12(O112),
    .O13(O113), .O14(O114), .O15(O115), .O16(O116), .O17(O117), .O18(O118), .O19(O119), .O20(O120),
    .O21(O121), .O22(O122), .O23(O123), .O24(O124));
  third4 third4_2 (
    .I1(in_65), .I2(in_66), .I3(in_67), .I4(in_68), .I5(in_69), .I6(in_70), .I7(in_71), .I8(in_72),
    .I9(in_73), .I10(in_74), .I11(in_75), .I12(in_76), .I13(in_77), .I14(in_78), .I15(in_79), .I16(in_80),
    .I17(in_81), .in_18(in_82), .in_19(in_83), .in_20(in_84), .in_21(in_85), .in_22(in_86), .in_23(in_87),
    .in_24(in_88), .in_25(in_89), .in_26(in_90), .in_27(in_91), .in_28(in_92), .in_29(in_93), .in_30(in_94),
    .in_31(in_95), .in_32(in_96), .I33(in_97), .in_34(in_98), .in_35(in_99), .in_36(in_100), .in_37(in_101),
    .in_38(in_102), .in_39(in_103), .in_40(in_104), .in_41(in_105), .in_42(in_106), .in_43(in_107),
    .in_44(in_108), .in_45(in_109), .in_46(in_110), .in_47(in_111), .in_48(in_112), .I49(in_113),
    .in_50(in_114), .in_51(in_115), .in_52(in_116), .in_53(in_117), .in_54(in_118), .in_55(in_119),
    .in_56(in_120), .in_57(in_121), .in_58(in_122), .in_59(in_123), .in_60(in_124), .in_61(in_125),
    .in_62(in_126), .in_63(in_127), .in_64(in_128), .O1(O21), .O2(O22), .O3(O23), .O4(O24), .O5(O25),
    .O6(O26), .O7(O27), .O8(O28), .O9(O29), .O10(O210), .O11(O211), .O12(O212), .O13(O213), .O14(O214),
    .O15(O215), .O16(O216), .O17(O217), .O18(O218), .O19(O219), .O20(O220), .O21(O221), .O22(O222),
    .O23(O223), .O24(O224));
  assign out_129 = O11 | O21;  // OR_Gate or_1, 24 bits wide
  assign out_130 = O12 | O22;  // OR_Gate or_2, 24 bits wide
  assign out_131 = O13 | O23;  // OR_Gate or_3, 24 bits wide
  assign out_132 = O14 | O24;  // OR_Gate or_4, 24 bits wide
  assign out_133 = O15 | O25;  // OR_Gate or_5, 24 bits wide
  assign out_134 = O16 | O26;  // OR_Gate or_6, 24 bits wide
  assign out_135 = O17 | O27;  // OR_Gate or_7, 24 bits wide
  assign out_136 = O18 | O28;  // OR_Gate or_8, 24 bits wide
  assign out_137 = O19 | O29;  // OR_Gate or_9, 24 bits wide
  assign out_138 = O110 | O210;  // OR_Gate or_10, 24 bits wide
  assign out_139 = O111 | O211;  // OR_Gate or_11, 24 bits wide
  assign out_140 = O112 | O212;  // OR_Gate or_12, 24 bits wide
  assign out_141 = O113 | O213;  // OR_Gate or_13, 24 bits wide
  assign out_142 = O114 | O214;  // OR_Gate or_14, 24 bits wide
  assign out_143 = O115 | O215;  // OR_Gate or_15, 24 bits wide
  assign out_144 = O116 | O216;  // OR_Gate or_16, 24 bits wide
  assign out_145 = O117 | O217;  // OR_Gate or_17, 24 bits wide
  assign out_146 = O118 | O218;  // OR_Gate or_18, 24 bits wide
  assign out_147 = O119 | O219;  // OR_Gate or_19, 24 bits wide
  assign out_148 = O120 | O220;  // OR_Gate or_20, 24 bits wide
  assign out_149 = O121 | O221;  // OR_Gate or_21, 24 bits wide
  assign out_150 = O122 | O222;  // OR_Gate or_22, 24 bits wide
  assign out_151 = O123 | O223;  // OR_Gate or_23, 24 bits wide
  assign out_152 = O124 | O224;  // OR_Gate or_24, 24 bits wide
endmodule

module xydemulti (
  input  [9:0] I,
  output [23:0] out_2,
  output [23:0] out_3,
  output [23:0] out_4,
  output [23:0] out_5,
  output [23:0] out_6,
  output [23:0] out_7,
  output [23:0] out_8,
  output [23:0] out_9,
  output [23:0] out_10,
  output [23:0] out_11,
  output [23:0] out_12,
  output [23:0] out_13,
  output [23:0] out_14,
  output [23:0] out_15,
  output [23:0] out_16,
  output [23:0] out_17,
  output [23:0] out_18,
  output [23:0] out_19,
  output [23:0] out_20,
  output [23:0] out_21,
  output [23:0] out_22,
  output [23:0] out_23,
  output [23:0] out_24,
  output [23:0] out_25
);

  wire [23:0] shifter_1_out;

  Shifter #(.width(24)) shifter_1 (.in(24'h1), .\dist (I[4:0]), .out(shifter_1_out));
  Demultiplexer #(.select(5), .width(24)) demultiplexer_1 (
    .out0(out_2), .out1(out_3), .out2(out_4), .out3(out_5), .out4(out_6), .out5(out_7), .out6(out_8),
    .out7(out_9), .out8(out_10), .out9(out_11), .out10(out_12), .out11(out_13), .out12(out_14),
    .out13(out_15), .out14(out_16), .out15(out_17), .out16(out_18), .out17(out_19), .out18(out_20),
    .out19(out_21), .out20(out_22), .out21(out_23), .out22(out_24), .out23(out_25), .in(shifter_1_out),
    .sel(I[9:5]));  // open: out24, out25, out26, out27, out28, out29, out30, out31
endmodule

module first4 (
  input  [9:0] I1,
  input  [9:0] I2,
  input  [9:0] I3,
  input  [9:0] I4,
  output [23:0] O1,
  output [23:0] O2,
  output [23:0] O3,
  output [23:0] O4,
  output [23:0] O5,
  output [23:0] O6,
  output [23:0] O7,
  output [23:0] O8,
  output [23:0] O9,
  output [23:0] O10,
  output [23:0] O11,
  output [23:0] O12,
  output [23:0] O13,
  output [23:0] O14,
  output [23:0] O15,
  output [23:0] O16,
  output [23:0] O17,
  output [23:0] O18,
  output [23:0] O19,
  output [23:0] O20,
  output [23:0] O21,
  output [23:0] O22,
  output [23:0] O23,
  output [23:0] O24
);

  wire [23:0] O11_t, O12_t, O13_t, O14_t, O15_t, O16_t, O17_t, O18_t, O19_t, O21_t, O22_t, O23_t, O24_t, O25,
       O26, O27, O28, O29, O31, O32, O33, O34, O35, O36, O37, O38, O39, O41, O42, O43, O44, O45, O46, O47,
       O48, O49, O110, O111, O112, O113, O114, O115, O116, O117, O118, O119, O120, O121, O122, O123, O124,
       O210, O211, O212, O213, O214, O215, O216, O217, O218, O219, O220, O221, O222, O223, O224, O310, O311,
       O312, O313, O314, O315, O316, O317, O318, O319, O320, O321, O322, O323, O324, O410, O411, O412, O413,
       O414, O415, O416, O417, O418, O419, O420, O421, O422, O423, O424;

  xydemulti xydemulti_1 (
    .I(I1), .out_2(O11_t), .out_3(O12_t), .out_4(O13_t), .out_5(O14_t), .out_6(O15_t), .out_7(O16_t),
    .out_8(O17_t), .out_9(O18_t), .out_10(O19_t), .out_11(O110), .out_12(O111), .out_13(O112), .out_14(O113),
    .out_15(O114), .out_16(O115), .out_17(O116), .out_18(O117), .out_19(O118), .out_20(O119), .out_21(O120),
    .out_22(O121), .out_23(O122), .out_24(O123), .out_25(O124));
  xydemulti xydemulti_2 (
    .I(I2), .out_2(O21_t), .out_3(O22_t), .out_4(O23_t), .out_5(O24_t), .out_6(O25), .out_7(O26),
    .out_8(O27), .out_9(O28), .out_10(O29), .out_11(O210), .out_12(O211), .out_13(O212), .out_14(O213),
    .out_15(O214), .out_16(O215), .out_17(O216), .out_18(O217), .out_19(O218), .out_20(O219), .out_21(O220),
    .out_22(O221), .out_23(O222), .out_24(O223), .out_25(O224));
  xydemulti xydemulti_3 (
    .I(I3), .out_2(O31), .out_3(O32), .out_4(O33), .out_5(O34), .out_6(O35), .out_7(O36), .out_8(O37),
    .out_9(O38), .out_10(O39), .out_11(O310), .out_12(O311), .out_13(O312), .out_14(O313), .out_15(O314),
    .out_16(O315), .out_17(O316), .out_18(O317), .out_19(O318), .out_20(O319), .out_21(O320), .out_22(O321),
    .out_23(O322), .out_24(O323), .out_25(O324));
  xydemulti xydemulti_4 (
    .I(I4), .out_2(O41), .out_3(O42), .out_4(O43), .out_5(O44), .out_6(O45), .out_7(O46), .out_8(O47),
    .out_9(O48), .out_10(O49), .out_11(O410), .out_12(O411), .out_13(O412), .out_14(O413), .out_15(O414),
    .out_16(O415), .out_17(O416), .out_18(O417), .out_19(O418), .out_20(O419), .out_21(O420), .out_22(O421),
    .out_23(O422), .out_24(O423), .out_25(O424));
  assign O1 = O11_t | O21_t | O31 | O41;  // OR_Gate or_1, 24 bits wide
  assign O2 = O12_t | O22_t | O32 | O42;  // OR_Gate or_2, 24 bits wide
  assign O3 = O13_t | O23_t | O33 | O43;  // OR_Gate or_3, 24 bits wide
  assign O4 = O14_t | O24_t | O34 | O44;  // OR_Gate or_4, 24 bits wide
  assign O5 = O15_t | O25 | O35 | O45;  // OR_Gate or_5, 24 bits wide
  assign O6 = O16_t | O26 | O36 | O46;  // OR_Gate or_6, 24 bits wide
  assign O7 = O17_t | O27 | O37 | O47;  // OR_Gate or_7, 24 bits wide
  assign O8 = O18_t | O28 | O38 | O48;  // OR_Gate or_8, 24 bits wide
  assign O9 = O19_t | O29 | O39 | O49;  // OR_Gate or_9, 24 bits wide
  assign O10 = O110 | O210 | O310 | O410;  // OR_Gate or_10, 24 bits wide
  assign O11 = O111 | O211 | O311 | O411;  // OR_Gate or_11, 24 bits wide
  assign O12 = O112 | O212 | O312 | O412;  // OR_Gate or_12, 24 bits wide
  assign O13 = O113 | O213 | O313 | O413;  // OR_Gate or_13, 24 bits wide
  assign O14 = O114 | O214 | O314 | O414;  // OR_Gate or_14, 24 bits wide
  assign O15 = O115 | O215 | O315 | O415;  // OR_Gate or_15, 24 bits wide
  assign O16 = O116 | O216 | O316 | O416;  // OR_Gate or_16, 24 bits wide
  assign O17 = O117 | O217 | O317 | O417;  // OR_Gate or_17, 24 bits wide
  assign O18 = O118 | O218 | O318 | O418;  // OR_Gate or_18, 24 bits wide
  assign O19 = O119 | O219 | O319 | O419;  // OR_Gate or_19, 24 bits wide
  assign O20 = O120 | O220 | O320 | O420;  // OR_Gate or_20, 24 bits wide
  assign O21 = O121 | O221 | O321 | O421;  // OR_Gate or_21, 24 bits wide
  assign O22 = O122 | O222 | O322 | O422;  // OR_Gate or_22, 24 bits wide
  assign O23 = O123 | O223 | O323 | O423;  // OR_Gate or_23, 24 bits wide
  assign O24 = O124 | O224 | O324 | O424;  // OR_Gate or_24, 24 bits wide
endmodule

module second4 (
  input  [9:0] I1,
  input  [9:0] I2,
  input  [9:0] I3,
  input  [9:0] I4,
  input  [9:0] I5,
  input  [9:0] I6,
  input  [9:0] I7,
  input  [9:0] I8,
  input  [9:0] I9,
  input  [9:0] I10,
  input  [9:0] I11,
  input  [9:0] I12,
  input  [9:0] I13,
  input  [9:0] I14,
  input  [9:0] I15,
  input  [9:0] I16,
  output [23:0] O1,
  output [23:0] O2,
  output [23:0] O3,
  output [23:0] O4,
  output [23:0] O5,
  output [23:0] O6,
  output [23:0] O7,
  output [23:0] O8,
  output [23:0] O9,
  output [23:0] O10,
  output [23:0] O11,
  output [23:0] O12,
  output [23:0] O13,
  output [23:0] O14,
  output [23:0] O15,
  output [23:0] O16,
  output [23:0] O17,
  output [23:0] O18,
  output [23:0] O19,
  output [23:0] O20,
  output [23:0] O21,
  output [23:0] O22,
  output [23:0] O23,
  output [23:0] O24
);

  wire [23:0] O11_t, O12_t, O13_t, O14_t, O15_t, O16_t, O17_t, O18_t, O19_t, O21_t, O22_t, O23_t, O24_t, O25,
       O26, O27, O28, O29, O31, O32, O33, O34, O35, O36, O37, O38, O39, O41, O42, O43, O44, O45, O46, O47,
       O48, O49, O110, O111, O112, O113, O114, O115, O116, O117, O118, O119, O120, O121, O122, O123, O124,
       O210, O211, O212, O213, O214, O215, O216, O217, O218, O219, O220, O221, O222, O223, O224, O310, O311,
       O312, O313, O314, O315, O316, O317, O318, O319, O320, O321, O322, O323, O324, O410, O411, O412, O413,
       O414, O415, O416, O417, O418, O419, O420, O421, O422, O423, O424;

  first4 first4_1 (
    .I1(I1), .I2(I2), .I3(I3), .I4(I4), .O1(O11_t), .O2(O12_t), .O3(O13_t), .O4(O14_t), .O5(O15_t),
    .O6(O16_t), .O7(O17_t), .O8(O18_t), .O9(O19_t), .O10(O110), .O11(O111), .O12(O112), .O13(O113),
    .O14(O114), .O15(O115), .O16(O116), .O17(O117), .O18(O118), .O19(O119), .O20(O120), .O21(O121),
    .O22(O122), .O23(O123), .O24(O124));
  first4 first4_2 (
    .I1(I5), .I2(I6), .I3(I7), .I4(I8), .O1(O21_t), .O2(O22_t), .O3(O23_t), .O4(O24_t), .O5(O25), .O6(O26),
    .O7(O27), .O8(O28), .O9(O29), .O10(O210), .O11(O211), .O12(O212), .O13(O213), .O14(O214), .O15(O215),
    .O16(O216), .O17(O217), .O18(O218), .O19(O219), .O20(O220), .O21(O221), .O22(O222), .O23(O223), .O24(O224));
  first4 first4_3 (
    .I1(I9), .I2(I10), .I3(I11), .I4(I12), .O1(O31), .O2(O32), .O3(O33), .O4(O34), .O5(O35), .O6(O36),
    .O7(O37), .O8(O38), .O9(O39), .O10(O310), .O11(O311), .O12(O312), .O13(O313), .O14(O314), .O15(O315),
    .O16(O316), .O17(O317), .O18(O318), .O19(O319), .O20(O320), .O21(O321), .O22(O322), .O23(O323), .O24(O324));
  first4 first4_4 (
    .I1(I13), .I2(I14), .I3(I15), .I4(I16), .O1(O41), .O2(O42), .O3(O43), .O4(O44), .O5(O45), .O6(O46),
    .O7(O47), .O8(O48), .O9(O49), .O10(O410), .O11(O411), .O12(O412), .O13(O413), .O14(O414), .O15(O415),
    .O16(O416), .O17(O417), .O18(O418), .O19(O419), .O20(O420), .O21(O421), .O22(O422), .O23(O423), .O24(O424));
  assign O1 = O11_t | O21_t | O31 | O41;  // OR_Gate or_1, 24 bits wide
  assign O2 = O12_t | O22_t | O32 | O42;  // OR_Gate or_2, 24 bits wide
  assign O3 = O13_t | O23_t | O33 | O43;  // OR_Gate or_3, 24 bits wide
  assign O4 = O14_t | O24_t | O34 | O44;  // OR_Gate or_4, 24 bits wide
  assign O5 = O15_t | O25 | O35 | O45;  // OR_Gate or_5, 24 bits wide
  assign O6 = O16_t | O26 | O36 | O46;  // OR_Gate or_6, 24 bits wide
  assign O7 = O17_t | O27 | O37 | O47;  // OR_Gate or_7, 24 bits wide
  assign O8 = O18_t | O28 | O38 | O48;  // OR_Gate or_8, 24 bits wide
  assign O9 = O19_t | O29 | O39 | O49;  // OR_Gate or_9, 24 bits wide
  assign O10 = O110 | O210 | O310 | O410;  // OR_Gate or_10, 24 bits wide
  assign O11 = O111 | O211 | O311 | O411;  // OR_Gate or_11, 24 bits wide
  assign O12 = O112 | O212 | O312 | O412;  // OR_Gate or_12, 24 bits wide
  assign O13 = O113 | O213 | O313 | O413;  // OR_Gate or_13, 24 bits wide
  assign O14 = O114 | O214 | O314 | O414;  // OR_Gate or_14, 24 bits wide
  assign O15 = O115 | O215 | O315 | O415;  // OR_Gate or_15, 24 bits wide
  assign O16 = O116 | O216 | O316 | O416;  // OR_Gate or_16, 24 bits wide
  assign O17 = O117 | O217 | O317 | O417;  // OR_Gate or_17, 24 bits wide
  assign O18 = O118 | O218 | O318 | O418;  // OR_Gate or_18, 24 bits wide
  assign O19 = O119 | O219 | O319 | O419;  // OR_Gate or_19, 24 bits wide
  assign O20 = O120 | O220 | O320 | O420;  // OR_Gate or_20, 24 bits wide
  assign O21 = O121 | O221 | O321 | O421;  // OR_Gate or_21, 24 bits wide
  assign O22 = O122 | O222 | O322 | O422;  // OR_Gate or_22, 24 bits wide
  assign O23 = O123 | O223 | O323 | O423;  // OR_Gate or_23, 24 bits wide
  assign O24 = O124 | O224 | O324 | O424;  // OR_Gate or_24, 24 bits wide
endmodule

module third4 (
  input  [9:0] I1,
  input  [9:0] I2,
  input  [9:0] I3,
  input  [9:0] I4,
  input  [9:0] I5,
  input  [9:0] I6,
  input  [9:0] I7,
  input  [9:0] I8,
  input  [9:0] I9,
  input  [9:0] I10,
  input  [9:0] I11,
  input  [9:0] I12,
  input  [9:0] I13,
  input  [9:0] I14,
  input  [9:0] I15,
  input  [9:0] I16,
  input  [9:0] I17,
  input  [9:0] in_18,
  input  [9:0] in_19,
  input  [9:0] in_20,
  input  [9:0] in_21,
  input  [9:0] in_22,
  input  [9:0] in_23,
  input  [9:0] in_24,
  input  [9:0] in_25,
  input  [9:0] in_26,
  input  [9:0] in_27,
  input  [9:0] in_28,
  input  [9:0] in_29,
  input  [9:0] in_30,
  input  [9:0] in_31,
  input  [9:0] in_32,
  input  [9:0] I33,
  input  [9:0] in_34,
  input  [9:0] in_35,
  input  [9:0] in_36,
  input  [9:0] in_37,
  input  [9:0] in_38,
  input  [9:0] in_39,
  input  [9:0] in_40,
  input  [9:0] in_41,
  input  [9:0] in_42,
  input  [9:0] in_43,
  input  [9:0] in_44,
  input  [9:0] in_45,
  input  [9:0] in_46,
  input  [9:0] in_47,
  input  [9:0] in_48,
  input  [9:0] I49,
  input  [9:0] in_50,
  input  [9:0] in_51,
  input  [9:0] in_52,
  input  [9:0] in_53,
  input  [9:0] in_54,
  input  [9:0] in_55,
  input  [9:0] in_56,
  input  [9:0] in_57,
  input  [9:0] in_58,
  input  [9:0] in_59,
  input  [9:0] in_60,
  input  [9:0] in_61,
  input  [9:0] in_62,
  input  [9:0] in_63,
  input  [9:0] in_64,
  output [23:0] O1,
  output [23:0] O2,
  output [23:0] O3,
  output [23:0] O4,
  output [23:0] O5,
  output [23:0] O6,
  output [23:0] O7,
  output [23:0] O8,
  output [23:0] O9,
  output [23:0] O10,
  output [23:0] O11,
  output [23:0] O12,
  output [23:0] O13,
  output [23:0] O14,
  output [23:0] O15,
  output [23:0] O16,
  output [23:0] O17,
  output [23:0] O18,
  output [23:0] O19,
  output [23:0] O20,
  output [23:0] O21,
  output [23:0] O22,
  output [23:0] O23,
  output [23:0] O24
);

  wire [23:0] O11_t, O12_t, O13_t, O14_t, O15_t, O16_t, O17_t, O18_t, O19_t, O21_t, O22_t, O23_t, O24_t, O25,
       O26, O27, O28, O29, O31, O32, O33, O34, O35, O36, O37, O38, O39, O41, O42, O43, O44, O45, O46, O47,
       O48, O49, O110, O111, O112, O113, O114, O115, O116, O117, O118, O119, O120, O121, O122, O123, O124,
       O210, O211, O212, O213, O214, O215, O216, O217, O218, O219, O220, O221, O222, O223, O224, O310, O311,
       O312, O313, O314, O315, O316, O317, O318, O319, O320, O321, O322, O323, O324, O410, O411, O412, O413,
       O414, O415, O416, O417, O418, O419, O420, O421, O422, O423, O424;

  second4 second4_1 (
    .I1(I1), .I2(I2), .I3(I3), .I4(I4), .I5(I5), .I6(I6), .I7(I7), .I8(I8), .I9(I9), .I10(I10), .I11(I11),
    .I12(I12), .I13(I13), .I14(I14), .I15(I15), .I16(I16), .O1(O11_t), .O2(O12_t), .O3(O13_t), .O4(O14_t),
    .O5(O15_t), .O6(O16_t), .O7(O17_t), .O8(O18_t), .O9(O19_t), .O10(O110), .O11(O111), .O12(O112),
    .O13(O113), .O14(O114), .O15(O115), .O16(O116), .O17(O117), .O18(O118), .O19(O119), .O20(O120),
    .O21(O121), .O22(O122), .O23(O123), .O24(O124));
  second4 second4_2 (
    .I1(I17), .I2(in_18), .I3(in_19), .I4(in_20), .I5(in_21), .I6(in_22), .I7(in_23), .I8(in_24), .I9(in_25),
    .I10(in_26), .I11(in_27), .I12(in_28), .I13(in_29), .I14(in_30), .I15(in_31), .I16(in_32), .O1(O21_t),
    .O2(O22_t), .O3(O23_t), .O4(O24_t), .O5(O25), .O6(O26), .O7(O27), .O8(O28), .O9(O29), .O10(O210),
    .O11(O211), .O12(O212), .O13(O213), .O14(O214), .O15(O215), .O16(O216), .O17(O217), .O18(O218),
    .O19(O219), .O20(O220), .O21(O221), .O22(O222), .O23(O223), .O24(O224));
  second4 second4_3 (
    .I1(I33), .I2(in_34), .I3(in_35), .I4(in_36), .I5(in_37), .I6(in_38), .I7(in_39), .I8(in_40), .I9(in_41),
    .I10(in_42), .I11(in_43), .I12(in_44), .I13(in_45), .I14(in_46), .I15(in_47), .I16(in_48), .O1(O31),
    .O2(O32), .O3(O33), .O4(O34), .O5(O35), .O6(O36), .O7(O37), .O8(O38), .O9(O39), .O10(O310), .O11(O311),
    .O12(O312), .O13(O313), .O14(O314), .O15(O315), .O16(O316), .O17(O317), .O18(O318), .O19(O319),
    .O20(O320), .O21(O321), .O22(O322), .O23(O323), .O24(O324));
  second4 second4_4 (
    .I1(I49), .I2(in_50), .I3(in_51), .I4(in_52), .I5(in_53), .I6(in_54), .I7(in_55), .I8(in_56), .I9(in_57),
    .I10(in_58), .I11(in_59), .I12(in_60), .I13(in_61), .I14(in_62), .I15(in_63), .I16(in_64), .O1(O41),
    .O2(O42), .O3(O43), .O4(O44), .O5(O45), .O6(O46), .O7(O47), .O8(O48), .O9(O49), .O10(O410), .O11(O411),
    .O12(O412), .O13(O413), .O14(O414), .O15(O415), .O16(O416), .O17(O417), .O18(O418), .O19(O419),
    .O20(O420), .O21(O421), .O22(O422), .O23(O423), .O24(O424));
  assign O1 = O11_t | O21_t | O31 | O41;  // OR_Gate or_1, 24 bits wide
  assign O2 = O12_t | O22_t | O32 | O42;  // OR_Gate or_2, 24 bits wide
  assign O3 = O13_t | O23_t | O33 | O43;  // OR_Gate or_3, 24 bits wide
  assign O4 = O14_t | O24_t | O34 | O44;  // OR_Gate or_4, 24 bits wide
  assign O5 = O15_t | O25 | O35 | O45;  // OR_Gate or_5, 24 bits wide
  assign O6 = O16_t | O26 | O36 | O46;  // OR_Gate or_6, 24 bits wide
  assign O7 = O17_t | O27 | O37 | O47;  // OR_Gate or_7, 24 bits wide
  assign O8 = O18_t | O28 | O38 | O48;  // OR_Gate or_8, 24 bits wide
  assign O9 = O19_t | O29 | O39 | O49;  // OR_Gate or_9, 24 bits wide
  assign O10 = O110 | O210 | O310 | O410;  // OR_Gate or_10, 24 bits wide
  assign O11 = O111 | O211 | O311 | O411;  // OR_Gate or_11, 24 bits wide
  assign O12 = O112 | O212 | O312 | O412;  // OR_Gate or_12, 24 bits wide
  assign O13 = O113 | O213 | O313 | O413;  // OR_Gate or_13, 24 bits wide
  assign O14 = O114 | O214 | O314 | O414;  // OR_Gate or_14, 24 bits wide
  assign O15 = O115 | O215 | O315 | O415;  // OR_Gate or_15, 24 bits wide
  assign O16 = O116 | O216 | O316 | O416;  // OR_Gate or_16, 24 bits wide
  assign O17 = O117 | O217 | O317 | O417;  // OR_Gate or_17, 24 bits wide
  assign O18 = O118 | O218 | O318 | O418;  // OR_Gate or_18, 24 bits wide
  assign O19 = O119 | O219 | O319 | O419;  // OR_Gate or_19, 24 bits wide
  assign O20 = O120 | O220 | O320 | O420;  // OR_Gate or_20, 24 bits wide
  assign O21 = O121 | O221 | O321 | O421;  // OR_Gate or_21, 24 bits wide
  assign O22 = O122 | O222 | O322 | O422;  // OR_Gate or_22, 24 bits wide
  assign O23 = O123 | O223 | O323 | O423;  // OR_Gate or_23, 24 bits wide
  assign O24 = O124 | O224 | O324 | O424;  // OR_Gate or_24, 24 bits wide
endmodule

module GPU (
  input  [1:0] inst,
  input  clk,
  input  Load,
  output [23:0] Column1,
  output [23:0] Column2,
  output [23:0] Column3,
  output [23:0] Column4,
  output [23:0] Column5,
  output [23:0] Column6,
  output [23:0] Column7,
  output [23:0] Column8,
  output [23:0] Column9,
  output [23:0] Column10,
  output [23:0] Column11,
  output [23:0] Column12,
  output [23:0] Column13,
  output [23:0] Column14,
  output [23:0] Column15,
  output [23:0] Column16,
  output [23:0] Column17,
  output [23:0] Column18,
  output [23:0] Column19,
  output [23:0] Column20,
  output [23:0] Column21,
  output [23:0] Column22,
  output [23:0] Column23,
  output [23:0] Column24
);

  wire [9:0] Cube_Coordinates_point1, Cube_Coordinates_point2, Cube_Coordinates_point3,
       Cube_Coordinates_point4, Cube_Coordinates_point5, Cube_Coordinates_point6, Cube_Coordinates_point7,
       Cube_Coordinates_point8, Cube_Coordinates_point9, Cube_Coordinates_point10, Cube_Coordinates_point11,
       Cube_Coordinates_point12, Cube_Coordinates_point13, Cube_Coordinates_point14,
       Cube_Coordinates_point15, Cube_Coordinates_point16, Cube_Coordinates_point17,
       Cube_Coordinates_point18, Cube_Coordinates_point19, Cube_Coordinates_point20,
       Cube_Coordinates_point21, Cube_Coordinates_point22, Cube_Coordinates_point23,
       Cube_Coordinates_point24, Cube_Coordinates_point25, Cube_Coordinates_point26,
       Cube_Coordinates_point27, Cube_Coordinates_point28, Cube_Coordinates_point29,
       Cube_Coordinates_point30, Cube_Coordinates_point31, Cube_Coordinates_point32,
       Cube_Coordinates_point33, Cube_Coordinates_point34, Cube_Coordinates_point35,
       Cube_Coordinates_point36, Cube_Coordinates_point37, Cube_Coordinates_point38,
       Cube_Coordinates_point39, Cube_Coordinates_point40, Cube_Coordinates_point41,
       Cube_Coordinates_point42, Cube_Coordinates_point43, Cube_Coordinates_point44,
       Cube_Coordinates_point45, Cube_Coordinates_point46, Cube_Coordinates_point47,
       Cube_Coordinates_point48, Cube_Coordinates_point49, Cube_Coordinates_point50,
       Cube_Coordinates_point51, Cube_Coordinates_point52, Cube_Coordinates_point53,
       Cube_Coordinates_point54, Cube_Coordinates_point55, Cube_Coordinates_point56,
       Cube_Coordinates_point57, Cube_Coordinates_point58, Cube_Coordinates_point59,
       Cube_Coordinates_point60, Cube_Coordinates_point61, Cube_Coordinates_point62,
       Cube_Coordinates_point63, Cube_Coordinates_point64, Cube_Coordinates_point65,
       Cube_Coordinates_point66, Cube_Coordinates_point67, Cube_Coordinates_point68,
       Cube_Coordinates_point69, Cube_Coordinates_point70, Cube_Coordinates_point71,
       Cube_Coordinates_point72, Cube_Coordinates_point73, Cube_Coordinates_point74,
       Cube_Coordinates_point75, Cube_Coordinates_point76, Cube_Coordinates_point77,
       Cube_Coordinates_point78, Cube_Coordinates_point79, Cube_Coordinates_point80,
       Cube_Coordinates_point81, Cube_Coordinates_point82, Cube_Coordinates_point83,
       Cube_Coordinates_point84, Cube_Coordinates_point85, Cube_Coordinates_point86,
       Cube_Coordinates_point87, Cube_Coordinates_point88, Cube_Coordinates_point89,
       Cube_Coordinates_point90, Cube_Coordinates_point91, Cube_Coordinates_point92,
       Cube_Coordinates_point93, Cube_Coordinates_point94, Cube_Coordinates_point95,
       Cube_Coordinates_point96, Cube_Coordinates_point97, Cube_Coordinates_point98,
       Cube_Coordinates_point99, Cube_Coordinates_point100, Cube_Coordinates_point101,
       Cube_Coordinates_point102, Cube_Coordinates_point103, Cube_Coordinates_point104,
       Cube_Coordinates_point105, Cube_Coordinates_point106, Cube_Coordinates_point107,
       Cube_Coordinates_point108, Cube_Coordinates_point109, Cube_Coordinates_point110,
       Cube_Coordinates_point111, Cube_Coordinates_point112, Cube_Coordinates_point113,
       Cube_Coordinates_point114, Cube_Coordinates_point115, Cube_Coordinates_point116,
       Cube_Coordinates_point117, Cube_Coordinates_point118, Cube_Coordinates_point119,
       Cube_Coordinates_point120, Cube_Coordinates_point121, Cube_Coordinates_point122,
       Cube_Coordinates_point123, Cube_Coordinates_point124, Cube_Coordinates_point125,
       Cube_Coordinates_point126, Cube_Coordinates_point127, Cube_Coordinates_point128;

  Pixel_Register Cube_Coordinates (
    .cmd(inst), .clock(clk), .Load(Load), .Point1(Cube_Coordinates_point1), .Point2(Cube_Coordinates_point2),
    .Point3(Cube_Coordinates_point3), .Point4(Cube_Coordinates_point4), .Point5(Cube_Coordinates_point5),
    .Point6(Cube_Coordinates_point6), .Point7(Cube_Coordinates_point7), .Point8(Cube_Coordinates_point8),
    .Point9(Cube_Coordinates_point9), .Point10(Cube_Coordinates_point10), .Point11(Cube_Coordinates_point11),
    .Point12(Cube_Coordinates_point12), .Point13(Cube_Coordinates_point13),
    .Point14(Cube_Coordinates_point14), .Point15(Cube_Coordinates_point15),
    .Point16(Cube_Coordinates_point16), .Point17(Cube_Coordinates_point17),
    .Point18(Cube_Coordinates_point18), .Point19(Cube_Coordinates_point19),
    .Point20(Cube_Coordinates_point20), .Point21(Cube_Coordinates_point21),
    .Point22(Cube_Coordinates_point22), .Point23(Cube_Coordinates_point23),
    .Point24(Cube_Coordinates_point24), .Point25(Cube_Coordinates_point25),
    .Point26(Cube_Coordinates_point26), .Point27(Cube_Coordinates_point27),
    .Point28(Cube_Coordinates_point28), .Point29(Cube_Coordinates_point29),
    .Point30(Cube_Coordinates_point30), .Point31(Cube_Coordinates_point31),
    .Point32(Cube_Coordinates_point32), .Point33(Cube_Coordinates_point33),
    .Point34(Cube_Coordinates_point34), .Point35(Cube_Coordinates_point35),
    .Point36(Cube_Coordinates_point36), .Point37(Cube_Coordinates_point37),
    .Point38(Cube_Coordinates_point38), .Point39(Cube_Coordinates_point39),
    .Point40(Cube_Coordinates_point40), .Point41(Cube_Coordinates_point41),
    .Point42(Cube_Coordinates_point42), .Point43(Cube_Coordinates_point43),
    .Point44(Cube_Coordinates_point44), .Point45(Cube_Coordinates_point45),
    .Point46(Cube_Coordinates_point46), .Point47(Cube_Coordinates_point47),
    .Point48(Cube_Coordinates_point48), .Point49(Cube_Coordinates_point49),
    .Point50(Cube_Coordinates_point50), .Point51(Cube_Coordinates_point51),
    .Point52(Cube_Coordinates_point52), .Point53(Cube_Coordinates_point53),
    .Point54(Cube_Coordinates_point54), .Point55(Cube_Coordinates_point55),
    .Point56(Cube_Coordinates_point56), .Point57(Cube_Coordinates_point57),
    .Point58(Cube_Coordinates_point58), .Point59(Cube_Coordinates_point59),
    .Point60(Cube_Coordinates_point60), .Point61(Cube_Coordinates_point61),
    .Point62(Cube_Coordinates_point62), .Point63(Cube_Coordinates_point63),
    .Point64(Cube_Coordinates_point64), .Point65(Cube_Coordinates_point65),
    .Point66(Cube_Coordinates_point66), .Point67(Cube_Coordinates_point67),
    .Point68(Cube_Coordinates_point68), .Point69(Cube_Coordinates_point69),
    .Point70(Cube_Coordinates_point70), .Point71(Cube_Coordinates_point71),
    .Point72(Cube_Coordinates_point72), .Point73(Cube_Coordinates_point73),
    .Point74(Cube_Coordinates_point74), .Point75(Cube_Coordinates_point75),
    .Point76(Cube_Coordinates_point76), .Point77(Cube_Coordinates_point77),
    .Point78(Cube_Coordinates_point78), .Point79(Cube_Coordinates_point79),
    .Point80(Cube_Coordinates_point80), .Point81(Cube_Coordinates_point81),
    .Point82(Cube_Coordinates_point82), .Point83(Cube_Coordinates_point83),
    .Point84(Cube_Coordinates_point84), .Point85(Cube_Coordinates_point85),
    .Point86(Cube_Coordinates_point86), .Point87(Cube_Coordinates_point87),
    .Point88(Cube_Coordinates_point88), .Point89(Cube_Coordinates_point89),
    .Point90(Cube_Coordinates_point90), .Point91(Cube_Coordinates_point91),
    .Point92(Cube_Coordinates_point92), .Point93(Cube_Coordinates_point93),
    .Point94(Cube_Coordinates_point94), .Point95(Cube_Coordinates_point95),
    .Point96(Cube_Coordinates_point96), .Point97(Cube_Coordinates_point97),
    .Point98(Cube_Coordinates_point98), .Point99(Cube_Coordinates_point99),
    .Point100(Cube_Coordinates_point100), .Point101(Cube_Coordinates_point101),
    .Point102(Cube_Coordinates_point102), .Point103(Cube_Coordinates_point103),
    .Point104(Cube_Coordinates_point104), .Point105(Cube_Coordinates_point105),
    .Point106(Cube_Coordinates_point106), .Point107(Cube_Coordinates_point107),
    .Point108(Cube_Coordinates_point108), .Point109(Cube_Coordinates_point109),
    .Point110(Cube_Coordinates_point110), .Point111(Cube_Coordinates_point111),
    .Point112(Cube_Coordinates_point112), .Point113(Cube_Coordinates_point113),
    .Point114(Cube_Coordinates_point114), .Point115(Cube_Coordinates_point115),
    .Point116(Cube_Coordinates_point116), .Point117(Cube_Coordinates_point117),
    .Point118(Cube_Coordinates_point118), .Point119(Cube_Coordinates_point119),
    .Point120(Cube_Coordinates_point120), .Point121(Cube_Coordinates_point121),
    .Point122(Cube_Coordinates_point122), .Point123(Cube_Coordinates_point123),
    .Point124(Cube_Coordinates_point124), .Point125(Cube_Coordinates_point125),
    .Point126(Cube_Coordinates_point126), .Point127(Cube_Coordinates_point127),
    .Point128(Cube_Coordinates_point128));
  Interpreter Coordinates_to_screen (
    .in_1(Cube_Coordinates_point1), .in_2(Cube_Coordinates_point2), .in_3(Cube_Coordinates_point3),
    .in_4(Cube_Coordinates_point4), .in_5(Cube_Coordinates_point5), .in_6(Cube_Coordinates_point6),
    .in_7(Cube_Coordinates_point7), .in_8(Cube_Coordinates_point8), .in_9(Cube_Coordinates_point9),
    .in_10(Cube_Coordinates_point10), .in_11(Cube_Coordinates_point11), .in_12(Cube_Coordinates_point12),
    .in_13(Cube_Coordinates_point13), .in_14(Cube_Coordinates_point14), .in_15(Cube_Coordinates_point15),
    .in_16(Cube_Coordinates_point16), .in_17(Cube_Coordinates_point17), .in_18(Cube_Coordinates_point18),
    .in_19(Cube_Coordinates_point19), .in_20(Cube_Coordinates_point20), .in_21(Cube_Coordinates_point21),
    .in_22(Cube_Coordinates_point22), .in_23(Cube_Coordinates_point23), .in_24(Cube_Coordinates_point24),
    .in_25(Cube_Coordinates_point25), .in_26(Cube_Coordinates_point26), .in_27(Cube_Coordinates_point27),
    .in_28(Cube_Coordinates_point28), .in_29(Cube_Coordinates_point29), .in_30(Cube_Coordinates_point30),
    .in_31(Cube_Coordinates_point31), .in_32(Cube_Coordinates_point32), .in_33(Cube_Coordinates_point33),
    .in_34(Cube_Coordinates_point34), .in_35(Cube_Coordinates_point35), .in_36(Cube_Coordinates_point36),
    .in_37(Cube_Coordinates_point37), .in_38(Cube_Coordinates_point38), .in_39(Cube_Coordinates_point39),
    .in_40(Cube_Coordinates_point40), .in_41(Cube_Coordinates_point41), .in_42(Cube_Coordinates_point42),
    .in_43(Cube_Coordinates_point43), .in_44(Cube_Coordinates_point44), .in_45(Cube_Coordinates_point45),
    .in_46(Cube_Coordinates_point46), .in_47(Cube_Coordinates_point47), .in_48(Cube_Coordinates_point48),
    .in_49(Cube_Coordinates_point49), .in_50(Cube_Coordinates_point50), .in_51(Cube_Coordinates_point51),
    .in_52(Cube_Coordinates_point52), .in_53(Cube_Coordinates_point53), .in_54(Cube_Coordinates_point54),
    .in_55(Cube_Coordinates_point55), .in_56(Cube_Coordinates_point56), .in_57(Cube_Coordinates_point57),
    .in_58(Cube_Coordinates_point58), .in_59(Cube_Coordinates_point59), .in_60(Cube_Coordinates_point60),
    .in_61(Cube_Coordinates_point61), .in_62(Cube_Coordinates_point62), .in_63(Cube_Coordinates_point63),
    .in_64(Cube_Coordinates_point64), .in_65(Cube_Coordinates_point65), .in_66(Cube_Coordinates_point66),
    .in_67(Cube_Coordinates_point67), .in_68(Cube_Coordinates_point68), .in_69(Cube_Coordinates_point69),
    .in_70(Cube_Coordinates_point70), .in_71(Cube_Coordinates_point71), .in_72(Cube_Coordinates_point72),
    .in_73(Cube_Coordinates_point73), .in_74(Cube_Coordinates_point74), .in_75(Cube_Coordinates_point75),
    .in_76(Cube_Coordinates_point76), .in_77(Cube_Coordinates_point77), .in_78(Cube_Coordinates_point78),
    .in_79(Cube_Coordinates_point79), .in_80(Cube_Coordinates_point80), .in_81(Cube_Coordinates_point81),
    .in_82(Cube_Coordinates_point82), .in_83(Cube_Coordinates_point83), .in_84(Cube_Coordinates_point84),
    .in_85(Cube_Coordinates_point85), .in_86(Cube_Coordinates_point86), .in_87(Cube_Coordinates_point87),
    .in_88(Cube_Coordinates_point88), .in_89(Cube_Coordinates_point89), .in_90(Cube_Coordinates_point90),
    .in_91(Cube_Coordinates_point91), .in_92(Cube_Coordinates_point92), .in_93(Cube_Coordinates_point93),
    .in_94(Cube_Coordinates_point94), .in_95(Cube_Coordinates_point95), .in_96(Cube_Coordinates_point96),
    .in_97(Cube_Coordinates_point97), .in_98(Cube_Coordinates_point98), .in_99(Cube_Coordinates_point99),
    .in_100(Cube_Coordinates_point100), .in_101(Cube_Coordinates_point101),
    .in_102(Cube_Coordinates_point102), .in_103(Cube_Coordinates_point103),
    .in_104(Cube_Coordinates_point104), .in_105(Cube_Coordinates_point105),
    .in_106(Cube_Coordinates_point106), .in_107(Cube_Coordinates_point107),
    .in_108(Cube_Coordinates_point108), .in_109(Cube_Coordinates_point109),
    .in_110(Cube_Coordinates_point110), .in_111(Cube_Coordinates_point111),
    .in_112(Cube_Coordinates_point112), .in_113(Cube_Coordinates_point113),
    .in_114(Cube_Coordinates_point114), .in_115(Cube_Coordinates_point115),
    .in_116(Cube_Coordinates_point116), .in_117(Cube_Coordinates_point117),
    .in_118(Cube_Coordinates_point118), .in_119(Cube_Coordinates_point119),
    .in_120(Cube_Coordinates_point120), .in_121(Cube_Coordinates_point121),
    .in_122(Cube_Coordinates_point122), .in_123(Cube_Coordinates_point123),
    .in_124(Cube_Coordinates_point124), .in_125(Cube_Coordinates_point125),
    .in_126(Cube_Coordinates_point126), .in_127(Cube_Coordinates_point127),
    .in_128(Cube_Coordinates_point128), .out_129(Column1), .out_130(Column2), .out_131(Column3),
    .out_132(Column4), .out_133(Column5), .out_134(Column6), .out_135(Column7), .out_136(Column8),
    .out_137(Column9), .out_138(Column10), .out_139(Column11), .out_140(Column12), .out_141(Column13),
    .out_142(Column14), .out_143(Column15), .out_144(Column16), .out_145(Column17), .out_146(Column18),
    .out_147(Column19), .out_148(Column20), .out_149(Column21), .out_150(Column22), .out_151(Column23),
    .out_152(Column24));
endmodule
